# Fritzing sketch follow_the_light (saved by Fritzing 0.9.3b)
breadboards: 1

parts:
  Componente1 = Arduino Uno (Rev3)
  LED1 = LED - 5mm [color="Red (633nm)" package="5 mm [THT]"]
  LED2 = LED - 5mm [color="Green (555nm)" package="5 mm [THT]"]
  LED3 = LED - 5mm [color="Green (555nm)" package="5 mm [THT]"]
  LED4 = LED - 5mm [color="Green (555nm)" package="5 mm [THT]"]
  R1 = Resistor [tolerance=±5% resistance=220 package=THT]
  R2 = Resistor [tolerance=±5% resistance=220 package=THT]
  R3 = Resistor [tolerance=±5% resistance=220 package=THT]
  R4 = Resistor [tolerance=±5% resistance=220 package=THT]
  S1 = Pushbutton [package="[THT]"]
  S2 = Pushbutton [package="[THT]"]
  S3 = Pushbutton [package="[THT]"]
  R5 = Resistor [tolerance=±5% resistance=10k package=THT]
  R6 = Resistor [tolerance=±5% resistance=10k package=THT]
  R7 = Resistor [tolerance=±5% resistance=10k package=THT]
  R8 = Rotary Potentiometer (Small) [maximum_resistance=100kΩ package=THT]

nets:
  N1: Componente1.A3, R8.wiper
  N2: Componente1.D8, R3.Pin_1
  N3: Componente1.D9_PWM, R2.Pin_1
  N4: Componente1.D10_PWM/SS, R1.Pin_1
  N5: Componente1.D11_PWM/MOSI, R4.Pin_1
  N6: Componente1.D2, S3.Pin_3, S3.Pin_4, R7.Pin_1
  N7: Componente1.D4, S2.Pin_3, S2.Pin_4, R6.Pin_1
  N8: Componente1.D5_PWM, S1.Pin_3, S1.Pin_4, R5.Pin_1
  N9: Componente1.5V, S1.Pin_1, S1.Pin_2, S2.Pin_1, S2.Pin_2, S3.Pin_1, S3.Pin_2, R8.leg2
  N10: Componente1.GND, LED1.cathode, LED2.cathode, LED3.cathode, LED4.cathode, R5.Pin_0, R6.Pin_0, R7.Pin_0, R8.leg1
  N11: LED1.anode, R4.Pin_0
  N12: LED2.anode, R3.Pin_0
  N13: LED3.anode, R2.Pin_0
  N14: LED4.anode, R1.Pin_0
